// Logisim project chipFullAdder.circ as structural Verilog: 1 circuit, main circuit main
module main (
  input  a,
  input  b,
  input  c,
  output sum,
  output out_5
);

  wire and_1_out, and_2_out, and_3_out, or_1_out, xor_1_out;

  xor xor_1 (xor_1_out, a, b);
  and and_1 (and_1_out, a, b);
  and and_2 (and_2_out, a, c);
  xor xor_2 (sum, xor_1_out, c);
  and and_3 (and_3_out, b, c);
  or or_1 (or_1_out, and_1_out, and_2_out);
  or or_2 (out_5, or_1_out, and_3_out);
endmodule
