// Logisim project otros(WaysMuxDmux).circ as structural Verilog: 10 circuits, main circuit DMUX
module DMUX (
  input  sel,
  input  in,
  output a,
  output b
);

  wire notSel_out;

  not notSel (notSel_out, sel);
  and AND (a, notSel_out, in);
  and AND_2 (b, sel, in);
endmodule

module _16_bitNot (
  input  [15:0] IN,
  output [15:0] OUT
);

  assign OUT[3:0] = ~IN[3:0];  // NOT_Gate not_1, 4 bits wide
  assign OUT[7:4] = ~IN[7:4];  // NOT_Gate not_2, 4 bits wide
  assign OUT[11:8] = ~IN[11:8];  // NOT_Gate not_3, 4 bits wide
  assign OUT[15:12] = ~IN[15:12];  // NOT_Gate not_4, 4 bits wide
endmodule

module AND16 (
  input  [15:0] a,
  input  [15:0] b,
  output [15:0] out
);

  assign out[3:0] = a[3:0] & b[3:0];  // AND_Gate and_1, 4 bits wide
  assign out[7:4] = a[7:4] & b[7:4];  // AND_Gate and_2, 4 bits wide
  assign out[11:8] = a[11:8] & b[11:8];  // AND_Gate and_3, 4 bits wide
  assign out[15:12] = a[15:12] & b[15:12];  // AND_Gate and_4, 4 bits wide
endmodule

module OR16 (
  input  [15:0] a,
  input  [15:0] b,
  output [15:0] out
);

  assign out[15:8] = a[15:8] | b[15:8];  // OR_Gate or_1, 8 bits wide
  assign out[7:0] = a[7:0] | b[7:0];  // OR_Gate or_2, 8 bits wide
endmodule

module MUX16 (
  input  [15:0] a,
  input  [15:0] b,
  input  sel,
  output [15:0] out
);

  Multiplexer #(.width(16), .enable("false")) multiplexer_1 (.in0(a), .in1(b), .out(out), .sel(sel));
endmodule

module _0R8WAY (
  input  in_1,
  input  in_2,
  input  in_3,
  input  in_4,
  input  in_5,
  input  in_6,
  input  in_7,
  input  in_8,
  output out_9
);

  wire or_1_out, or_2_out, or_3_out, or_4_out, or_5_out, or_6_out;

  or or_1 (or_1_out, in_1, in_2);
  or or_2 (or_2_out, or_1_out, in_3);
  or or_3 (or_3_out, or_2_out, in_4);
  or or_4 (or_4_out, or_3_out, in_5);
  or or_5 (or_5_out, or_4_out, in_6);
  or or_6 (or_6_out, or_5_out, in_7);
  or or_7 (out_9, or_6_out, in_8);
endmodule

module DMUX4 (
  input  IN,
  input  SEL_1,
  input  SEL_0,
  output A,
  output B,
  output C,
  output D
);

  wire demultiplexer_1_out0, demultiplexer_1_out1;

  Demultiplexer #(.enable("false")) demultiplexer_1 (
    .out0(demultiplexer_1_out0), .out1(demultiplexer_1_out1), .in(IN), .sel(SEL_1));
  Demultiplexer #(.enable("false")) demultiplexer_2 (.out0(A), .out1(B), .in(demultiplexer_1_out0), .sel(SEL_0));
  Demultiplexer #(.enable("false")) demultiplexer_3 (.out0(C), .out1(D), .in(demultiplexer_1_out1), .sel(SEL_0));
endmodule

module DMUX8 (
  input  IN,
  input  SEL_1,
  input  SEL_0,
  input  SEL_2,
  output A,
  output B,
  output C,
  output D,
  output E,
  output F,
  output G,
  output H
);

  wire demultiplexer_1_out0, demultiplexer_1_out1, demultiplexer_2_out0, demultiplexer_2_out1,
       demultiplexer_3_out0, demultiplexer_3_out1;

  Demultiplexer #(.enable("false")) demultiplexer_1 (
    .out0(demultiplexer_1_out0), .out1(demultiplexer_1_out1), .in(IN), .sel(SEL_2));
  Demultiplexer #(.enable("false")) demultiplexer_2 (
    .out0(demultiplexer_2_out0), .out1(demultiplexer_2_out1), .in(demultiplexer_1_out0), .sel(SEL_1));
  Demultiplexer #(.enable("false")) demultiplexer_3 (
    .out0(demultiplexer_3_out0), .out1(demultiplexer_3_out1), .in(demultiplexer_1_out1), .sel(SEL_1));
  Demultiplexer #(.enable("false")) demultiplexer_4 (.out0(A), .out1(B), .in(demultiplexer_2_out0), .sel(SEL_0));
  Demultiplexer #(.enable("false")) demultiplexer_5 (.out0(C), .out1(D), .in(demultiplexer_2_out1), .sel(SEL_0));
  Demultiplexer #(.enable("false")) demultiplexer_6 (.out0(E), .out1(F), .in(demultiplexer_3_out0), .sel(SEL_0));
  Demultiplexer #(.enable("false")) demultiplexer_7 (.out0(G), .out1(H), .in(demultiplexer_3_out1), .sel(SEL_0));
endmodule

module MUX8W16 (
  input  [15:0] A,
  input  [15:0] B,
  input  [15:0] C,
  input  SEL_1,
  input  [15:0] D,
  input  SEL_0,
  input  SEL_2,
  input  [15:0] E,
  input  [15:0] F,
  input  [15:0] G,
  input  [15:0] H,
  output [15:0] OUT
);

  wire [15:0] multiplexer_1_out, multiplexer_2_out, multiplexer_3_out, multiplexer_4_out, multiplexer_5_out,
       multiplexer_6_out;

  Multiplexer #(.width(16), .enable("false")) multiplexer_1 (.in0(A), .in1(B), .out(multiplexer_1_out), .sel(SEL_0));
  Multiplexer #(.width(16), .enable("false")) multiplexer_2 (.in0(C), .in1(D), .out(multiplexer_2_out), .sel(SEL_0));
  Multiplexer #(.width(16), .enable("false")) multiplexer_3 (.in0(E), .in1(F), .out(multiplexer_3_out), .sel(SEL_0));
  Multiplexer #(.width(16), .enable("false")) multiplexer_4 (.in0(G), .in1(H), .out(multiplexer_4_out), .sel(SEL_0));
  Multiplexer #(.width(16), .enable("false")) multiplexer_5 (
    .in0(multiplexer_1_out), .in1(multiplexer_2_out), .out(multiplexer_5_out), .sel(SEL_1));
  Multiplexer #(.width(16), .enable("false")) multiplexer_6 (
    .in0(multiplexer_3_out), .in1(multiplexer_4_out), .out(multiplexer_6_out), .sel(SEL_1));
  Multiplexer #(.width(16), .enable("false")) multiplexer_7 (
    .in0(multiplexer_5_out), .in1(multiplexer_6_out), .out(OUT), .sel(SEL_2));
endmodule

module MUX4W16 (
  input  [15:0] A,
  input  [15:0] B,
  input  [15:0] in_3,
  input  SEL_1,
  input  [15:0] in_5,
  input  SEL_0,
  output [15:0] out_7
);

  wire [15:0] multiplexer_1_out, multiplexer_2_out;

  Multiplexer #(.width(16), .enable("false")) multiplexer_1 (.in0(A), .in1(B), .out(multiplexer_1_out), .sel(SEL_0));
  Multiplexer #(.width(16), .enable("false")) multiplexer_2 (
    .in0(in_3), .in1(in_5), .out(multiplexer_2_out), .sel(SEL_0));
  Multiplexer #(.width(16), .enable("false")) multiplexer_3 (
    .in0(multiplexer_1_out), .in1(multiplexer_2_out), .out(out_7), .sel(SEL_1));
endmodule
