// Logisim project regsandram.circ as structural Verilog
// info.bit
module \bit  (
  input  entrada,
  input  load,
  output bit_almacenado
);

  wire clock_1_out, multiplexer_1_out;

  Multiplexer multiplexer_1 (.in0(bit_almacenado), .in1(entrada), .out(multiplexer_1_out), .sel(load));  // open: en
  Clock clock_1 (.out(clock_1_out));
  D_Flip_Flop d_ff_1 (.clk(clock_1_out), .D(multiplexer_1_out), .Q(bit_almacenado));  // open: Qn, preset, en, reset
endmodule

module registro (
  input  load,
  input  [15:0] in_2,
  output [15:0] out_3
);

  wire gclock;

  Clock clock_1 (.out(gclock));
  \bit  bit_1 (.entrada(in_2[0]), .load(load), .bit_almacenado(out_3[0]));
  \bit  bit_2 (.entrada(in_2[1]), .load(load), .bit_almacenado(out_3[1]));
  \bit  bit_3 (.entrada(in_2[2]), .load(load), .bit_almacenado(out_3[2]));
  \bit  bit_4 (.entrada(in_2[3]), .load(load), .bit_almacenado(out_3[3]));
  \bit  bit_5 (.entrada(in_2[4]), .load(load), .bit_almacenado(out_3[4]));
  \bit  bit_6 (.entrada(in_2[5]), .load(load), .bit_almacenado(out_3[5]));
  \bit  bit_7 (.entrada(in_2[6]), .load(load), .bit_almacenado(out_3[6]));
  \bit  bit_8 (.entrada(in_2[7]), .load(load), .bit_almacenado(out_3[7]));
  \bit  bit_9 (.entrada(in_2[8]), .load(load), .bit_almacenado(out_3[8]));
  \bit  bit_10 (.entrada(in_2[9]), .load(load), .bit_almacenado(out_3[9]));
  \bit  bit_11 (.entrada(in_2[10]), .load(load), .bit_almacenado(out_3[10]));
  \bit  bit_12 (.entrada(in_2[11]), .load(load), .bit_almacenado(out_3[11]));
  \bit  bit_13 (.entrada(in_2[12]), .load(load), .bit_almacenado(out_3[12]));
  \bit  bit_14 (.entrada(in_2[13]), .load(load), .bit_almacenado(out_3[13]));
  \bit  bit_15 (.entrada(in_2[14]), .load(load), .bit_almacenado(out_3[14]));
  \bit  bit_16 (.entrada(in_2[15]), .load(load), .bit_almacenado(out_3[15]));
endmodule

module shiftleft (
  input  in_1,
  input  [1:0] in_2,
  output [2:0] out_3
);


  assign out_3 = {in_2, in_1};
endmodule

module dmux8way_para_RAMS (
  input  sel_1,
  input  sel_0,
  input  in_3,
  input  sel_2,
  output out_5,
  output out_6,
  output out_7,
  output out_8,
  output out_9,
  output out_10,
  output out_11,
  output out_12
);

  wire demultiplexer_1_out0, demultiplexer_1_out1, demultiplexer_2_out0, demultiplexer_2_out1,
       demultiplexer_3_out0, demultiplexer_3_out1;

  Demultiplexer #(.enable("false")) demultiplexer_1 (
    .out0(demultiplexer_1_out0), .out1(demultiplexer_1_out1), .in(in_3), .sel(sel_2));
  Demultiplexer #(.enable("false")) demultiplexer_2 (
    .out0(demultiplexer_2_out0), .out1(demultiplexer_2_out1), .in(demultiplexer_1_out1), .sel(sel_1));
  Demultiplexer #(.enable("false")) demultiplexer_3 (
    .out0(demultiplexer_3_out0), .out1(demultiplexer_3_out1), .in(demultiplexer_1_out0), .sel(sel_1));
  Demultiplexer #(.enable("false")) demultiplexer_4 (
    .out0(out_5), .out1(out_6), .in(demultiplexer_3_out0), .sel(sel_0));
  Demultiplexer #(.enable("false")) demultiplexer_5 (
    .out0(out_7), .out1(out_8), .in(demultiplexer_3_out1), .sel(sel_0));
  Demultiplexer #(.enable("false")) demultiplexer_6 (
    .out0(out_9), .out1(out_10), .in(demultiplexer_2_out0), .sel(sel_0));
  Demultiplexer #(.enable("false")) demultiplexer_7 (
    .out0(out_11), .out1(out_12), .in(demultiplexer_2_out1), .sel(sel_0));

  // Notes on the sheet:
  //   Este circuito ya estaba hecho pero se hizo en otro archivo entonces toca implementarlo de nuevo.
endmodule

module mux8way16_para_RAMS (
  input  [15:0] in_1,
  input  [15:0] in_2,
  input  [15:0] in_3,
  input  [15:0] in_4,
  input  sel_0,
  input  sel_1,
  input  [15:0] in_7,
  input  sel_2,
  input  [15:0] in_9,
  input  [15:0] in_10,
  input  [15:0] in_11,
  output [15:0] out_12
);

  wire [15:0] multiplexer_1_out, multiplexer_2_out, multiplexer_3_out, multiplexer_4_out, multiplexer_5_out,
       multiplexer_6_out;

  Multiplexer #(.width(16), .enable("false")) multiplexer_1 (
    .in0(in_1), .in1(in_2), .out(multiplexer_1_out), .sel(sel_0));
  Multiplexer #(.width(16), .enable("false")) multiplexer_2 (
    .in0(in_3), .in1(in_4), .out(multiplexer_2_out), .sel(sel_0));
  Multiplexer #(.width(16), .enable("false")) multiplexer_3 (
    .in0(in_7), .in1(in_9), .out(multiplexer_3_out), .sel(sel_0));
  Multiplexer #(.width(16), .enable("false")) multiplexer_4 (
    .in0(in_10), .in1(in_11), .out(multiplexer_4_out), .sel(sel_0));
  Multiplexer #(.width(16), .enable("false")) multiplexer_5 (
    .in0(multiplexer_1_out), .in1(multiplexer_2_out), .out(multiplexer_5_out), .sel(sel_1));
  Multiplexer #(.width(16), .enable("false")) multiplexer_6 (
    .in0(multiplexer_3_out), .in1(multiplexer_4_out), .out(multiplexer_6_out), .sel(sel_1));
  Multiplexer #(.width(16), .enable("false")) multiplexer_7 (
    .in0(multiplexer_5_out), .in1(multiplexer_6_out), .out(out_12), .sel(sel_2));

  // Notes on the sheet:
  //   Este circuito ya estaba hecho pero se hizo en otro archivo entonces toca implementarlo de nuevo.
endmodule

// dmux8way16
module dmux8way_con_splitter (
  input  in_1,
  input  [2:0] sel_3bits,
  output out_3,
  output out_4,
  output out_5,
  output out_6,
  output out_7,
  output out_8,
  output out_9,
  output out_10
);

  wire demultiplexer_1_out0, demultiplexer_1_out1, demultiplexer_2_out0, demultiplexer_2_out1,
       demultiplexer_3_out0, demultiplexer_3_out1;

  Demultiplexer #(.enable("false")) demultiplexer_1 (
    .out0(demultiplexer_1_out0), .out1(demultiplexer_1_out1), .in(in_1), .sel(sel_3bits[2]));
  Demultiplexer #(.enable("false")) demultiplexer_2 (
    .out0(demultiplexer_2_out0), .out1(demultiplexer_2_out1), .in(demultiplexer_1_out1), .sel(sel_3bits[1]));
  Demultiplexer #(.enable("false")) demultiplexer_3 (
    .out0(demultiplexer_3_out0), .out1(demultiplexer_3_out1), .in(demultiplexer_1_out0), .sel(sel_3bits[1]));
  Demultiplexer #(.enable("false")) demultiplexer_4 (
    .out0(out_3), .out1(out_4), .in(demultiplexer_3_out0), .sel(sel_3bits[0]));
  Demultiplexer #(.enable("false")) demultiplexer_5 (
    .out0(out_5), .out1(out_6), .in(demultiplexer_3_out1), .sel(sel_3bits[0]));
  Demultiplexer #(.enable("false")) demultiplexer_6 (
    .out0(out_7), .out1(out_8), .in(demultiplexer_2_out0), .sel(sel_3bits[0]));
  Demultiplexer #(.enable("false")) demultiplexer_7 (
    .out0(out_9), .out1(out_10), .in(demultiplexer_2_out1), .sel(sel_3bits[0]));
endmodule

module RAM8__intento2 (
  input  [15:0] in_1,
  input  in_2,
  input  [2:0] in_3,
  input  [2:0] in_4,
  output [15:0] out_5
);

  wire clock_1_out, demultiplexer_1_out0, demultiplexer_1_out1, demultiplexer_1_out2, demultiplexer_1_out3,
       demultiplexer_1_out4, demultiplexer_1_out5, demultiplexer_1_out6, demultiplexer_1_out7;
  wire [15:0] register_1_q, register_2_q, register_3_q, register_4_q, register_5_q, register_6_q,
       register_7_q, register_8_q;

  Demultiplexer #(.select(3), .enable("false")) demultiplexer_1 (
    .out0(demultiplexer_1_out0), .out1(demultiplexer_1_out1), .out2(demultiplexer_1_out2),
    .out3(demultiplexer_1_out3), .out4(demultiplexer_1_out4), .out5(demultiplexer_1_out5),
    .out6(demultiplexer_1_out6), .out7(demultiplexer_1_out7), .in(in_2), .sel(in_4));
  Clock clock_1 (.out(clock_1_out));
  Register #(.width(16)) register_1 (
    .D(in_1), .en(demultiplexer_1_out0), .Q(register_1_q), .clk(clock_1_out));  // open: clr
  Register #(.width(16)) register_2 (
    .D(in_1), .en(demultiplexer_1_out1), .Q(register_2_q), .clk(clock_1_out));  // open: clr
  Register #(.width(16)) register_3 (
    .D(in_1), .en(demultiplexer_1_out2), .Q(register_3_q), .clk(clock_1_out));  // open: clr
  Register #(.width(16)) register_4 (
    .D(in_1), .en(demultiplexer_1_out3), .Q(register_4_q), .clk(clock_1_out));  // open: clr
  Register #(.width(16)) register_5 (
    .D(in_1), .en(demultiplexer_1_out4), .Q(register_5_q), .clk(clock_1_out));  // open: clr
  Register #(.width(16)) register_6 (
    .D(in_1), .en(demultiplexer_1_out5), .Q(register_6_q), .clk(clock_1_out));  // open: clr
  Register #(.width(16)) register_7 (
    .D(in_1), .en(demultiplexer_1_out6), .Q(register_7_q), .clk(clock_1_out));  // open: clr
  Register #(.width(16)) register_8 (
    .D(in_1), .en(demultiplexer_1_out7), .Q(register_8_q), .clk(clock_1_out));  // open: clr
  Multiplexer #(.select(3), .width(16), .enable("false")) multiplexer_1 (
    .in0(register_1_q), .in1(register_2_q), .in2(register_3_q), .in3(register_4_q), .in4(register_5_q),
    .in5(register_6_q), .in6(register_7_q), .in7(register_8_q), .out(out_5), .sel(in_3));
endmodule

module RAM64 (
  input  [15:0] in_1,
  input  load,
  input  [5:0] address,
  output [15:0] out_4
);

  wire demultiplexer_1_out0, demultiplexer_1_out1, demultiplexer_1_out2, demultiplexer_1_out3,
       demultiplexer_1_out4, demultiplexer_1_out5, demultiplexer_1_out6, demultiplexer_1_out7, gclock;
  wire [15:0] ram8_intento2_1_out_5, ram8_intento2_2_out_5, ram8_intento2_3_out_5, ram8_intento2_4_out_5,
       ram8_intento2_5_out_5, ram8_intento2_6_out_5, ram8_intento2_7_out_5, ram8_intento2_8_out_5;

  Clock clock_1 (.out(gclock));
  Demultiplexer #(.select(3), .enable("false")) demultiplexer_1 (
    .out0(demultiplexer_1_out0), .out1(demultiplexer_1_out1), .out2(demultiplexer_1_out2),
    .out3(demultiplexer_1_out3), .out4(demultiplexer_1_out4), .out5(demultiplexer_1_out5),
    .out6(demultiplexer_1_out6), .out7(demultiplexer_1_out7), .in(load), .sel(address[5:3]));
  RAM8__intento2 ram8_intento2_1 (
    .in_1(in_1), .in_2(demultiplexer_1_out0), .in_3(address[2:0]), .in_4(address[5:3]),
    .out_5(ram8_intento2_1_out_5));
  RAM8__intento2 ram8_intento2_2 (
    .in_1(in_1), .in_2(demultiplexer_1_out1), .in_3(address[2:0]), .in_4(address[5:3]),
    .out_5(ram8_intento2_2_out_5));
  RAM8__intento2 ram8_intento2_3 (
    .in_1(in_1), .in_2(demultiplexer_1_out2), .in_3(address[2:0]), .out_5(ram8_intento2_3_out_5));  // open: in_4
  RAM8__intento2 ram8_intento2_4 (
    .in_1(in_1), .in_2(demultiplexer_1_out3), .in_3(address[2:0]), .in_4(address[5:3]),
    .out_5(ram8_intento2_4_out_5));
  RAM8__intento2 ram8_intento2_5 (
    .in_1(in_1), .in_2(demultiplexer_1_out4), .in_3(address[2:0]), .in_4(address[5:3]),
    .out_5(ram8_intento2_5_out_5));
  RAM8__intento2 ram8_intento2_6 (
    .in_1(in_1), .in_2(demultiplexer_1_out5), .in_3(address[2:0]), .in_4(address[5:3]),
    .out_5(ram8_intento2_6_out_5));
  RAM8__intento2 ram8_intento2_7 (
    .in_1(in_1), .in_2(demultiplexer_1_out6), .in_3(address[2:0]), .in_4(address[5:3]),
    .out_5(ram8_intento2_7_out_5));
  RAM8__intento2 ram8_intento2_8 (
    .in_1(in_1), .in_2(demultiplexer_1_out7), .in_3(address[2:0]), .in_4(address[5:3]),
    .out_5(ram8_intento2_8_out_5));
  Multiplexer #(.select(3), .width(16), .enable("false")) multiplexer_1 (
    .in0(ram8_intento2_1_out_5), .in1(ram8_intento2_2_out_5), .in2(ram8_intento2_3_out_5),
    .in3(ram8_intento2_4_out_5), .in4(ram8_intento2_5_out_5), .in5(ram8_intento2_6_out_5),
    .in6(ram8_intento2_7_out_5), .in7(ram8_intento2_8_out_5), .out(out_4), .sel(address[5:3]));

  // Notes on the sheet:
  //   3 primeros bits - cual ram
  //   3 ultimos bits - cual de los 8 regs de esa ram
endmodule
