// Logisim project todosadders+alu+otros.circ as structural Verilog: 8 circuits, main circuit Adder16bits
module Adder16bits (
  input  CarryIn,
  input  [15:0] input_1__16bits,
  input  [15:0] input_2_16bits,
  output [15:0] Sum,
  output CarryOut
);

  wire fulladder_1_carryout, fulladder_2_carryout, fulladder_3_carryout, fulladder_4_carryout,
       fulladder_5_carryout, fulladder_6_carryout, fulladder_7_carryout, fulladder_8_carryout,
       fulladder_9_carryout, fulladder_10_carryout, fulladder_11_carryout, fulladder_12_carryout,
       fulladder_13_carryout, fulladder_14_carryout, fulladder_15_carryout;

  fulladder fulladder_1 (
    .a(input_1__16bits[0]), .b(input_2_16bits[0]), .carryIn(CarryIn), .carryout(fulladder_1_carryout),
    .sum(Sum[0]));
  fulladder fulladder_2 (
    .a(input_1__16bits[1]), .b(input_2_16bits[1]), .carryIn(fulladder_1_carryout),
    .carryout(fulladder_2_carryout), .sum(Sum[1]));
  fulladder fulladder_3 (
    .a(input_1__16bits[2]), .b(input_2_16bits[2]), .carryIn(fulladder_2_carryout),
    .carryout(fulladder_3_carryout), .sum(Sum[2]));
  fulladder fulladder_4 (
    .a(input_1__16bits[3]), .b(input_2_16bits[3]), .carryIn(fulladder_3_carryout),
    .carryout(fulladder_4_carryout), .sum(Sum[3]));
  fulladder fulladder_5 (
    .a(input_1__16bits[4]), .b(input_2_16bits[4]), .carryIn(fulladder_4_carryout),
    .carryout(fulladder_5_carryout), .sum(Sum[4]));
  fulladder fulladder_6 (
    .a(input_1__16bits[5]), .b(input_2_16bits[5]), .carryIn(fulladder_5_carryout),
    .carryout(fulladder_6_carryout), .sum(Sum[5]));
  fulladder fulladder_7 (
    .a(input_1__16bits[6]), .b(input_2_16bits[6]), .carryIn(fulladder_6_carryout),
    .carryout(fulladder_7_carryout), .sum(Sum[6]));
  fulladder fulladder_8 (
    .a(input_1__16bits[7]), .b(input_2_16bits[7]), .carryIn(fulladder_7_carryout),
    .carryout(fulladder_8_carryout), .sum(Sum[7]));
  fulladder fulladder_9 (
    .a(input_1__16bits[8]), .b(input_2_16bits[8]), .carryIn(fulladder_8_carryout),
    .carryout(fulladder_9_carryout), .sum(Sum[8]));
  fulladder fulladder_10 (
    .a(input_2_16bits[9]), .b(input_1__16bits[9]), .carryIn(fulladder_9_carryout),
    .carryout(fulladder_10_carryout), .sum(Sum[9]));
  fulladder fulladder_11 (
    .a(input_2_16bits[10]), .b(input_1__16bits[10]), .carryIn(fulladder_10_carryout),
    .carryout(fulladder_11_carryout), .sum(Sum[10]));
  fulladder fulladder_12 (
    .a(input_2_16bits[11]), .b(input_1__16bits[11]), .carryIn(fulladder_11_carryout),
    .carryout(fulladder_12_carryout), .sum(Sum[11]));
  fulladder fulladder_13 (
    .a(input_2_16bits[12]), .b(input_1__16bits[12]), .carryIn(fulladder_12_carryout),
    .carryout(fulladder_13_carryout), .sum(Sum[12]));
  fulladder fulladder_14 (
    .a(input_2_16bits[13]), .b(input_1__16bits[13]), .carryIn(fulladder_13_carryout),
    .carryout(fulladder_14_carryout), .sum(Sum[13]));
  fulladder fulladder_15 (
    .a(input_2_16bits[14]), .b(input_1__16bits[14]), .carryIn(fulladder_14_carryout),
    .carryout(fulladder_15_carryout), .sum(Sum[14]));
  fulladder fulladder_16 (
    .a(input_2_16bits[15]), .b(input_1__16bits[15]), .carryIn(fulladder_15_carryout), .carryout(CarryOut),
    .sum(Sum[15]));

  // Notes on the sheet:
  //   sumador completo numeros de 16 bits
endmodule

// sum
module fulladder (
  input  a,
  input  b,
  input  carryIn,
  output carryout,
  output sum
);

  wire halfadder_1_carry, halfadder_1_suma, halfadder_2_carry;

  halfadder halfadder_1 (.A(a), .B(b), .suma(halfadder_1_suma), .Carry(halfadder_1_carry));
  halfadder halfadder_2 (.A(halfadder_1_suma), .B(carryIn), .suma(sum), .Carry(halfadder_2_carry));
  or or_1 (carryout, halfadder_1_carry, halfadder_2_carry);
endmodule

module halfadder (
  input  A,
  input  B,
  output suma,
  output Carry
);

  xor xor_1 (suma, A, B);
  and and_1 (Carry, A, B);
endmodule

module Inc16__1 (
  input  CarryIn,
  input  [15:0] input_1__16bits,
  input  [15:0] input_2__16bits,
  output [15:0] out_4,
  output CarryOut
);

  wire fulladder_1_sum, fulladder_2_sum, fulladder_3_sum, fulladder_4_sum, fulladder_5_sum, fulladder_6_sum,
       fulladder_7_sum, fulladder_8_sum, fulladder_9_sum, fulladder_10_sum, fulladder_11_sum,
       fulladder_12_sum, fulladder_13_sum, fulladder_14_sum, fulladder_15_sum;

  fulladder fulladder_1 (
    .a(CarryIn), .b(input_1__16bits[0]), .carryIn(input_2__16bits[0]), .carryout(out_4[0]),
    .sum(fulladder_1_sum));
  fulladder fulladder_2 (
    .a(fulladder_1_sum), .b(input_1__16bits[1]), .carryIn(input_2__16bits[1]), .carryout(out_4[1]),
    .sum(fulladder_2_sum));
  fulladder fulladder_3 (
    .a(fulladder_2_sum), .b(input_1__16bits[2]), .carryIn(input_2__16bits[2]), .carryout(out_4[2]),
    .sum(fulladder_3_sum));
  fulladder fulladder_4 (
    .a(fulladder_3_sum), .b(input_1__16bits[3]), .carryIn(input_2__16bits[3]), .carryout(out_4[3]),
    .sum(fulladder_4_sum));
  fulladder fulladder_5 (
    .a(fulladder_4_sum), .b(input_1__16bits[4]), .carryIn(input_2__16bits[4]), .carryout(out_4[4]),
    .sum(fulladder_5_sum));
  fulladder fulladder_6 (
    .a(fulladder_5_sum), .b(input_1__16bits[5]), .carryIn(input_2__16bits[5]), .carryout(out_4[5]),
    .sum(fulladder_6_sum));
  fulladder fulladder_7 (
    .a(fulladder_6_sum), .b(input_1__16bits[6]), .carryIn(input_2__16bits[6]), .carryout(out_4[6]),
    .sum(fulladder_7_sum));
  fulladder fulladder_8 (
    .a(fulladder_7_sum), .b(input_1__16bits[7]), .carryIn(input_2__16bits[7]), .carryout(out_4[7]),
    .sum(fulladder_8_sum));
  fulladder fulladder_9 (
    .a(fulladder_8_sum), .b(input_1__16bits[8]), .carryIn(input_2__16bits[8]), .carryout(out_4[8]),
    .sum(fulladder_9_sum));
  fulladder fulladder_10 (
    .a(fulladder_9_sum), .b(input_1__16bits[9]), .carryIn(input_2__16bits[9]), .carryout(out_4[9]),
    .sum(fulladder_10_sum));
  fulladder fulladder_11 (
    .a(fulladder_10_sum), .b(input_1__16bits[10]), .carryIn(input_2__16bits[10]), .carryout(out_4[10]),
    .sum(fulladder_11_sum));
  fulladder fulladder_12 (
    .a(fulladder_11_sum), .b(input_1__16bits[11]), .carryIn(input_2__16bits[11]), .carryout(out_4[11]),
    .sum(fulladder_12_sum));
  fulladder fulladder_13 (
    .a(fulladder_12_sum), .b(input_1__16bits[12]), .carryIn(input_2__16bits[12]), .carryout(out_4[12]),
    .sum(fulladder_13_sum));
  fulladder fulladder_14 (
    .a(fulladder_13_sum), .b(input_1__16bits[13]), .carryIn(input_2__16bits[13]), .carryout(out_4[13]),
    .sum(fulladder_14_sum));
  fulladder fulladder_15 (
    .a(fulladder_14_sum), .b(input_1__16bits[14]), .carryIn(input_2__16bits[14]), .carryout(out_4[14]),
    .sum(fulladder_15_sum));
  fulladder fulladder_16 (
    .a(fulladder_15_sum), .b(input_1__16bits[15]), .carryIn(input_2__16bits[15]), .carryout(out_4[15]),
    .sum(CarryOut));

  // Notes on the sheet:
  //   settear a 1
endmodule

module Negador (
  input  [15:0] in_1,
  output [15:0] out_2
);

  not not_1 (out_2[0], in_1[0]);
  not not_2 (out_2[1], in_1[1]);
  not not_3 (out_2[2], in_1[2]);
  not not_4 (out_2[3], in_1[3]);
  not not_5 (out_2[4], in_1[4]);
  not not_6 (out_2[5], in_1[5]);
  not not_7 (out_2[6], in_1[6]);
  not not_8 (out_2[7], in_1[7]);
  not not_9 (out_2[8], in_1[8]);
  not not_10 (out_2[9], in_1[9]);
  not not_11 (out_2[10], in_1[10]);
  not not_12 (out_2[11], in_1[11]);
  not not_13 (out_2[12], in_1[12]);
  not not_14 (out_2[13], in_1[13]);
  not not_15 (out_2[14], in_1[14]);
  not not_16 (out_2[15], in_1[15]);
endmodule

// zy
module ALU (
  input  [15:0] inputx_16bits,
  input  [15:0] in_2,
  input  nx,
  input  zx,
  input  no,
  input  f,
  input  [15:0] input_y_16bits,
  input  [15:0] in_8,
  input  ny,
  input  zy,
  input  CarryIn_0___suma,
  output ng,
  output zr,
  output [15:0] out
);

  wire or16way_para_alu_1_out_2;
  wire [15:0] adder16bits_1_sum, and16_outand16, multiplexer_1_out, multiplexer_2_out, multiplexer_3_out,
       multiplexer_4_out, multiplexer_5_out, negador_1_out_2, negador_2_out_2, negador_3_out_2;

  Multiplexer #(.width(16), .enable("false")) multiplexer_1 (
    .in0(inputx_16bits), .in1(in_2), .out(multiplexer_1_out), .sel(zx));
  Multiplexer #(.width(16), .enable("false")) multiplexer_2 (
    .in0(input_y_16bits), .in1(in_8), .out(multiplexer_2_out), .sel(zy));
  Negador negador_1 (.in_1(multiplexer_1_out), .out_2(negador_1_out_2));
  Negador negador_2 (.in_1(multiplexer_2_out), .out_2(negador_2_out_2));
  Multiplexer #(.width(16), .enable("false")) multiplexer_3 (
    .in0(multiplexer_1_out), .in1(negador_1_out_2), .out(multiplexer_3_out), .sel(nx));
  Multiplexer #(.width(16), .enable("false")) multiplexer_4 (
    .in0(multiplexer_2_out), .in1(negador_2_out_2), .out(multiplexer_4_out), .sel(ny));
  AND16_PARA_ALU and16 (.input1(multiplexer_4_out), .input2(multiplexer_3_out), .outAND16(and16_outand16));
  Adder16bits adder16bits_1 (
    .CarryIn(CarryIn_0___suma), .input_1__16bits(multiplexer_3_out), .input_2_16bits(multiplexer_4_out),
    .Sum(adder16bits_1_sum));  // open: CarryOut
  Multiplexer #(.width(16), .enable("false")) multiplexer_5 (
    .in0(and16_outand16), .in1(adder16bits_1_sum), .out(multiplexer_5_out), .sel(f));
  Negador negador_3 (.in_1(multiplexer_5_out), .out_2(negador_3_out_2));
  Multiplexer #(.width(16), .enable("false")) multiplexer_6 (
    .in0(multiplexer_5_out), .in1(negador_3_out_2), .out({ng, out[14:0]}), .sel(no));
  not not_1 (zr, or16way_para_alu_1_out_2);
  OR16WAY_PARA_ALU or16way_para_alu_1 (.in_1({ng, out[14:0]}), .out_2(or16way_para_alu_1_out_2));

  assign out[15] = ng;

  // Notes on the sheet:
  //   cero
  //   cero
endmodule

module AND16_PARA_ALU (
  input  [15:0] input1,
  input  [15:0] input2,
  output [15:0] outAND16
);

  and and_1 (outAND16[0], input1[0], input2[0]);
  and and_2 (outAND16[1], input1[1], input2[1]);
  and and_3 (outAND16[2], input1[2], input2[2]);
  and and_4 (outAND16[3], input1[3], input2[3]);
  and and_5 (outAND16[4], input1[4], input2[4]);
  and and_6 (outAND16[5], input1[5], input2[5]);
  and and_7 (outAND16[6], input1[6], input2[6]);
  and and_8 (outAND16[7], input1[7], input2[7]);
  and and_9 (outAND16[8], input1[8], input2[8]);
  and and_10 (outAND16[9], input1[9], input2[9]);
  and and_11 (outAND16[10], input1[10], input2[10]);
  and and_12 (outAND16[11], input1[11], input2[11]);
  and and_13 (outAND16[12], input1[12], input2[12]);
  and and_14 (outAND16[13], input1[13], input2[13]);
  and and_15 (outAND16[14], input1[14], input2[14]);
  and and_16 (outAND16[15], input1[15], input2[15]);
endmodule

module OR16WAY_PARA_ALU (
  input  [15:0] in_1,
  output out_2
);

  wire or_1_out, or_2_out, or_3_out, or_4_out, or_5_out, or_6_out, or_7_out, or_8_out, or_9_out, or_10_out,
       or_11_out, or_12_out, or_13_out, or_14_out;

  or or_1 (or_1_out, in_1[0], in_1[1]);
  or or_2 (or_2_out, in_1[2], in_1[3]);
  or or_3 (or_3_out, in_1[4], in_1[5]);
  or or_4 (or_4_out, in_1[6], in_1[7]);
  or or_5 (or_5_out, in_1[8], in_1[9]);
  or or_6 (or_6_out, in_1[10], in_1[11]);
  or or_7 (or_7_out, in_1[12], in_1[13]);
  or or_8 (or_8_out, in_1[14], in_1[15]);
  or or_9 (or_9_out, or_1_out, or_2_out);
  or or_10 (or_10_out, or_3_out, or_4_out);
  or or_11 (or_11_out, or_5_out, or_6_out);
  or or_12 (or_12_out, or_7_out, or_8_out);
  or or_13 (or_13_out, or_9_out, or_10_out);
  or or_14 (or_14_out, or_11_out, or_12_out);
  or or_15 (out_2, or_13_out, or_14_out);
endmodule
